// Logisim project LUT_v2.circ as structural Verilog: 6 circuits, main circuit main
module main (
  input  in_1,
  input  in_2,
  input  in_3,
  input  in_4,
  input  in_5,
  input  in_6,
  input  [7:0] in_7,
  input  [1:0] SC1,
  input  [1:0] SC1_2,
  input  [1:0] SC2,
  input  [1:0] SC2_2,
  input  [1:0] SC3,
  input  [1:0] SC3_2,
  input  in_14,
  input  in_15,
  input  in_16,
  input  in_17,
  input  in_18,
  input  in_19,
  input  [7:0] in_20,
  input  [7:0] in_21,
  input  [1:0] SC1_3,
  input  [1:0] SC1_4,
  input  [1:0] SC2_3,
  input  [1:0] SC2_4,
  input  [1:0] SC3_3,
  input  [1:0] SC3_4,
  output Sum,
  output Carry,
  output out_30,
  output out_31
);

  wire [7:0] sipo_8bit_1_pop;

  sipo_8bit sipo_8bit_1 (.Pop(sipo_8bit_1_pop));  // open: Scl, Sip, Rcl
  lut_switch L0 (
    .Config_bits(sipo_8bit_1_pop), .SM1({out_31, Carry, out_30, in_6}), .SM2({out_31, Carry, out_30, in_5}),
    .SM3({out_31, Carry, out_30, in_4}), .SC1(SC1), .SC2(SC2), .SC3(SC3), .Y(Sum));
  lut_switch L2 (
    .Config_bits(in_20), .SM1({out_31, Carry, Sum, in_16}), .SM2({out_31, Carry, Sum, in_15}),
    .SM3({out_31, Carry, Sum, in_14}), .SC1(SC1_3), .SC2(SC2_3), .SC3(SC3_3), .Y(out_30));
  lut_switch L1 (
    .Config_bits(in_7), .SM1({out_31, out_30, Sum, in_3}), .SM2({out_31, out_30, Sum, in_2}),
    .SM3({out_31, out_30, Sum, in_1}), .SC1(SC1_2), .SC2(SC2_2), .SC3(SC3_2), .Y(Carry));
  lut_switch L3 (
    .Config_bits(in_21), .SM1({Carry, out_30, Sum, in_19}), .SM2({Carry, out_30, Sum, in_18}),
    .SM3({Carry, out_30, Sum, in_17}), .SC1(SC1_4), .SC2(SC2_4), .SC3(SC3_4), .Y(out_31));
endmodule

module LUT_v2 (
  input  [7:0] Config_bits,
  input  IP1,
  input  IP2,
  input  IP3,
  output out_5
);

  Multiplexer #(.select(3), .enable("false")) multiplexer_1 (
    .in0(Config_bits[0]), .in1(Config_bits[1]), .in2(Config_bits[2]), .in3(Config_bits[3]),
    .in4(Config_bits[4]), .in5(Config_bits[5]), .in6(Config_bits[6]), .in7(Config_bits[7]), .out(out_5),
    .sel({IP1, IP2, IP3}));
endmodule

module Switch_matrix (
  input  [3:0] SM,
  input  [1:0] SC,
  output out_3
);

  Multiplexer #(.select(2), .enable("false")) multiplexer_1 (
    .in0(SM[0]), .in1(SM[1]), .in2(SM[2]), .in3(SM[3]), .out(out_3), .sel(SC));
endmodule

module lut_switch (
  input  [7:0] Config_bits,
  input  [3:0] SM1,
  input  [3:0] SM2,
  input  [3:0] SM3,
  input  [1:0] SC1,
  input  [1:0] SC2,
  input  [1:0] SC3,
  output Y
);

  wire switch_matrix_1_out_3, switch_matrix_2_out_3, switch_matrix_3_out_3;

  Switch_matrix switch_matrix_1 (.SM(SM1), .SC(SC1), .out_3(switch_matrix_1_out_3));
  Switch_matrix switch_matrix_2 (.SM(SM2), .SC(SC2), .out_3(switch_matrix_2_out_3));
  Switch_matrix switch_matrix_3 (.SM(SM3), .SC(SC3), .out_3(switch_matrix_3_out_3));
  LUT_v2 lut_v2_1 (
    .Config_bits(Config_bits), .IP1(switch_matrix_1_out_3), .IP2(switch_matrix_2_out_3),
    .IP3(switch_matrix_3_out_3), .out_5(Y));
endmodule

module Tristate_matrix (
  input  [2:0] Control,
  input  [2:0] Data,
  output out_3,
  output out_4,
  output out_5
);

  assign out_3 = Control[0] ? Data[0] : 1'bz;  // Controlled_Buffer controlled_buffer_1
  assign out_4 = Control[1] ? Data[1] : 1'bz;  // Controlled_Buffer controlled_buffer_2
  assign out_5 = Control[2] ? Data[2] : 1'bz;  // Controlled_Buffer controlled_buffer_3
endmodule

module sipo_8bit (
  input  Scl,
  input  Sip,
  input  Rcl,
  output [7:0] Pop
);

  wire d_ff_1_q, d_ff_3_q, d_ff_5_q, d_ff_7_q, d_ff_9_q, d_ff_11_q, d_ff_12_q, d_ff_14_q;

  D_Flip_Flop d_ff_1 (.D(Sip), .clk(Rcl), .Q(d_ff_1_q));  // open: Qn, preset, reset
  D_Flip_Flop d_ff_2 (.D(d_ff_1_q), .clk(Scl), .Q(Pop[7]));  // open: Qn, preset, reset
  D_Flip_Flop d_ff_3 (.D(d_ff_1_q), .clk(Rcl), .Q(d_ff_3_q));  // open: Qn, preset, reset
  D_Flip_Flop d_ff_4 (.D(d_ff_3_q), .clk(Scl), .Q(Pop[6]));  // open: Qn, preset, reset
  D_Flip_Flop d_ff_5 (.D(d_ff_3_q), .clk(Rcl), .Q(d_ff_5_q));  // open: Qn, preset, reset
  D_Flip_Flop d_ff_6 (.D(d_ff_5_q), .clk(Scl), .Q(Pop[5]));  // open: Qn, preset, reset
  D_Flip_Flop d_ff_7 (.D(d_ff_5_q), .clk(Rcl), .Q(d_ff_7_q));  // open: Qn, preset, reset
  D_Flip_Flop d_ff_8 (.D(d_ff_7_q), .clk(Scl), .Q(Pop[4]));  // open: Qn, preset, reset
  D_Flip_Flop d_ff_9 (.D(d_ff_7_q), .clk(Rcl), .Q(d_ff_9_q));  // open: Qn, preset, reset
  D_Flip_Flop d_ff_10 (.D(d_ff_9_q), .clk(Scl), .Q(Pop[3]));  // open: Qn, preset, reset
  D_Flip_Flop d_ff_11 (.D(d_ff_9_q), .clk(Rcl), .Q(d_ff_11_q));  // open: Qn, preset, reset
  D_Flip_Flop d_ff_12 (.D(d_ff_11_q), .clk(Rcl), .Q(d_ff_12_q));  // open: Qn, preset, reset
  D_Flip_Flop d_ff_13 (.D(d_ff_11_q), .clk(Scl), .Q(Pop[2]));  // open: Qn, preset, reset
  D_Flip_Flop d_ff_14 (.D(d_ff_12_q), .clk(Rcl), .Q(d_ff_14_q));  // open: Qn, preset, reset
  D_Flip_Flop d_ff_15 (.D(d_ff_12_q), .clk(Scl), .Q(Pop[1]));  // open: Qn, preset, reset
  D_Flip_Flop d_ff_16 (.D(d_ff_14_q), .clk(Scl), .Q(Pop[0]));  // open: Qn, preset, reset
endmodule
